# Fritzing sketch paperweight (saved by Fritzing 0.9.2b)
breadboards: 2

parts:
  LCD1 = LCD screen
  R1 = Rotary Potentiometer (Small) [maximum_resistance=100kΩ package=THT]
  U1 = 74HC595 [package="DIP16 [THT]"]
  LED2 = LED - 5mm [color="Red (633nm)" package="5 mm [THT]"]
  LED3 = LED - 5mm [color="Red (633nm)" package="5 mm [THT]"]
  LED4 = LED - 5mm [color="Yellow (595nm)" package="5 mm [THT]"]
  LED5 = LED - 5mm [color="Yellow (595nm)" package="5 mm [THT]"]
  LED6 = LED - 5mm [color="Green (560nm)" package="5 mm [THT]"]
  LED7 = LED - 5mm [color="Green (560nm)" package="5 mm [THT]"]
  R2 = Resistor [tolerance=±5% resistance=330 package=THT]
  R3 = Resistor [tolerance=±5% resistance=330 package=THT]
  R4 = Resistor [tolerance=±5% resistance=330 package=THT]
  R5 = Resistor [tolerance=±5% resistance=330 package=THT]
  R6 = Resistor [tolerance=±5% resistance=330 package=THT]
  R7 = Resistor [tolerance=±5% resistance=330 package=THT]
  R8 = Resistor [tolerance=±5% resistance=330 package=THT]
  LED1 = LED - 5mm [color="Red (633nm)" package="5 mm [THT]"]
  Part1 = Arduino Uno (Rev3)

nets:
  GND: LCD1.VSS, LCD1.R/W, R1.leg2, U1.GND, U1.OE, R2.Pin_1, R3.Pin_1, R4.Pin_1, R5.Pin_1, R6.Pin_1, R7.Pin_1, R8.Pin_1, Part1.GND
  5V: LCD1.VDD, R1.leg1, U1.MR, U1.VCC, Part1.5V
  N1: LCD1.V0, R1.wiper
  RS: LCD1.RS, Part1.D12/MISO
  E: LCD1.E, Part1.D11_PWM/MOSI
  D4: LCD1.DB4, Part1.D7
  D5: LCD1.DB5, Part1.D8
  D6: LCD1.DB6, Part1.D9_PWM
  D8: LCD1.DB7, Part1.D10_PWM/SS
  N2: U1.Q1, LED1.anode
  N3: U1.Q2, LED2.anode
  N4: U1.Q3, LED3.anode
  N5: U1.Q4, LED4.anode
  N6: U1.Q5, LED5.anode
  N7: U1.Q6, LED6.anode
  N8: U1.Q7, LED7.anode
  PIN_CLOCK: U1.SH_CP, Part1.D2
  PIN_LATCH: U1.ST_CP, Part1.D3_PWM
  PIN_DATA: U1.DS, Part1.D4
  N9: LED2.cathode, R3.Pin_0
  N10: LED3.cathode, R4.Pin_0
  N11: LED4.cathode, R5.Pin_0
  N12: LED5.cathode, R6.Pin_0
  N13: LED6.cathode, R7.Pin_0
  N14: LED7.cathode, R8.Pin_0
  N15: R2.Pin_0, LED1.cathode
